# Fritzing sketch multiznachok (saved by Fritzing 0.9.2b)

parts:
  Lilypad = Lilypad Arduino Board
  Power_supply = LilyPad LiPower
  Previous_button = LilyPad Button Board
  Next_button = LilyPad Button Board
  Status_led = LilyPad LED
  EPD_connector = Header 8 [package=1x08_smd]

nets:
  GND: Lilypad.GND, Power_supply.GND, Previous_button.-, Next_button.-, Status_led.-, EPD_connector.7
  N1: Lilypad.ISCP_MOSI, Lilypad.MOSI/D11, EPD_connector.6
  N2: Lilypad.A0, Previous_button.S
  N3: Lilypad.A1, Next_button.S
  N4: Lilypad.D8, EPD_connector.2
  N5: Lilypad.D9, EPD_connector.3
  N6: Lilypad.D10, EPD_connector.4
  N7: Lilypad.SCK/D13, EPD_connector.5
  N8: Lilypad.D3, Status_led.+
  N9: Lilypad.D7, EPD_connector.1
  N10: Lilypad.VCC, Power_supply.+, EPD_connector.8

notes:
  Waveshare epd1in54b pinout (left to right):
  busy rst dc cs clk din gnd vcc
  Waveshare epd1in54b pinout (top to bottom):
  busy rst dc cs clk din gnd vcc
